# Fritzing sketch FM Modulator Demodulator_EE460 Lab_FinalProject (saved by Fritzing 0.9.4)
circuit board: 20.634cm x 12.0351cm
breadboards: 1

parts:
  IC1_LM565CN = IC, DIP package, 14 pins [chip_label="IC LM 565CN"]
  TRS1_3_5mm_Stereo_Audio_Jack_AUDIO_INPUT = Audio Jack (TRS) 3.5mm [package="PG203J [THT]"]
  R2_5_6K = 1K Ω Resistor [tolerance=±5% part_number="5.6K 5%" package=THT]
  R1_5_6K = 1K Ω Resistor [tolerance=±5% part_number="5.6K 5%" package=THT]
  C1_10uF_25V = Capacitor Polarized [part_number="10UF 25V" package=cpol-radial-10uf-25v]
  C2_10nF = Capacitor [package=cap-pth-small2]
  C3_100nF = Capacitor [package=cap-pth-small2]
  C5 = Capacitor Polarized [part_number="10uF 25V" package=cpol-radial-10uf-25v]
  R4_4_7K = 1K Ω Resistor [package=THT]
  R5_4_7K = 1K Ω Resistor [package=THT]
  R3_1K = 1K Ω Resistor [package=THT]
  R6_10K = 1K Ω Resistor [package=THT]
  R7_10K = 1K Ω Resistor [package=THT]
  R8_47K = 1K Ω Resistor [package=THT]
  R9_10_ohms = 1K Ω Resistor [package=THT]
  C8 = Capacitor Polarized [part_number=".1uF 100V" package=cpol-radial-10uf-25v]
  C9 = Capacitor Polarized [part_number="10uF 50V" package=cpol-radial-10uf-25v]
  R10_22K = 1K Ω Resistor [package=THT]
  JACK1 = 2.1mm Barrel Jack with Terminal Block [part_number=+15V]
  R12_10_Ohms = 1K Ω Resistor [package=THT]
  R13_1K = 1K Ω Resistor [package=THT]
  R14_4_7K = 1K Ω Resistor [package=THT]
  C11 = Capacitor Polarized [part_number=".1uF 100V" package=cpol-radial-10uf-25v]
  R15_10K = 1K Ω Resistor [package=THT]
  R16_10K = 1K Ω Resistor [package=THT]
  R17_4_7K = 1K Ω Resistor [package=THT]
  R18_2_2K = 1K Ω Resistor [package=THT]
  R19_1K = 1K Ω Resistor [package=THT]
  C11_1nF = Capacitor [package=cap-pth-small2]
  C12_470pF = Capacitor [package=cap-pth-small2]
  U1_500K = POT [package=pot_alpha_rv16af-20]
  U2_500K = POT [package=pot_alpha_rv16af-20]
  U3_500K = POT [package=pot_alpha_rv16af-20]
  IC2_LM565CN = IC, DIP package, 14 pins [chip_label="IC LM565CN"]
  C10_0_1uF = Capacitor [package=cap-pth-small2]
  C13_0_1uF = Capacitor [package=cap-pth-small2]
  C3_47pF = Capacitor [package=cap-pth-small2]
  C4_47pF = Capacitor [package=cap-pth-small2]
  C6_150pF = Capacitor [package=cap-pth-small2]
  C7_2_1nF = Capacitor [package=cap-pth-small2]
  IC3_LM380/NTE740A = IC, DIP package, 14 pins [chip_label=IC part_number="LM380/NTE 740A"]
  U4_500K = POT [part_number=500K package=pot_alpha_rv16af-20]
  C14_4_7uF_50V = Electrolytic Capacitor [package="100 mil [THT, electrolytic]"]
  C15_10uF_50V = Electrolytic Capacitor [package="100 mil [THT, electrolytic]"]
  C16_100uF_16V = Electrolytic Capacitor [package="100 mil [THT, electrolytic]"]
  C17_10nF = Capacitor [package=cap-pth-small2]
  C18_560uF = Electrolytic Capacitor [package="100 mil [THT, electrolytic]"]
  C20_100nF = Capacitor [package=cap-pth-small2]
  C21_100nF = Capacitor [package=cap-pth-small2]
  C22_100nF = Capacitor [package=cap-pth-small2]
  C23_100nF = Capacitor [package=cap-pth-small2]
  R20_2_7ohms = 1K Ω Resistor [package=THT]
  C19_47nF = Capacitor [package=cap-pth-small2]
  R21_20Mega = 1K Ω Resistor [package=THT]
  R22_22Mega = 1K Ω Resistor [package=THT]
  R23_22Mega = 1K Ω Resistor [package=THT]
  R24_22Mega = 1K Ω Resistor [package=THT]
  JACK2 = 2.1mm Barrel Jack with Terminal Block [part_number=-15V]
  U4_QUAD_OP_AMP = OP482 - Low Power, High Speed JFET Quad Operational Amplifier [part_number=OP482]
  U5 = POT [part_number=100K package=pot_alpha_rv16af-20]
  U6_500K = POT [part_number=500K package=pot_alpha_rv16af-20]
  C24_1nF = Capacitor [package=cap-pth-small2]
  C25_1nF = Capacitor [package=cap-pth-small2]
  R26_9K = 1K Ω Resistor [package=THT]
  R27_17K = 1K Ω Resistor [package=THT]
  R25_9K = 1K Ω Resistor [package=THT]
  R28_82K = 1K Ω Resistor [package=THT]
  R29_80K = 1K Ω Resistor [package=THT]
  R30_160K = 1K Ω Resistor [package=THT]
  C26_1nF = Capacitor [package=cap-pth-small2]
  C27_1nF = Capacitor [package=cap-pth-small2]
  U7_100K = POT [package=pot_alpha_rv16af-20]
  C28_1nF = Capacitor [package=cap-pth-small2]
  C29_1nF = Capacitor [package=cap-pth-small2]
  R31_18K = 1K Ω Resistor [package=THT]
  R32_8K = 1K Ω Resistor [package=THT]
  R33_8K = 1K Ω Resistor [package=THT]
  U8_1Meg = POT [package=pot_alpha_rv16af-20]
  C30_100nF = Capacitor [package=cap-pth-small2]
  C31_100nF = Capacitor [package=cap-pth-small2]
  R34_160K = 1K Ω Resistor [package=THT]
  R36_80K = 1K Ω Resistor [package=THT]
  R35_80K = 1K Ω Resistor [package=THT]
  TRS2_OUTPUT_FOR_25W_AMPLIFIER_BOARD = Audio Jack (TRS) 3.5mm [package="PG203J [THT]"]

nets:
  N1: IC1_LM565CN.pin2, IC1_LM565CN.pin3, R4_4_7K.Pin_0, R5_4_7K.Pin_1
  N2: IC1_LM565CN.pin4, C8.+
  N3: IC1_LM565CN.pin7, R3_1K.Pin_0, U2_500K.S
  N4: IC1_LM565CN.pin8, R18_2_2K.Pin_1
  N5: IC1_LM565CN.pin10, R5_4_7K.Pin_0, R9_10_ohms.Pin_1, JACK1.POS, R12_10_Ohms.Pin_0, R18_2_2K.Pin_0, R19_1K.Pin_0, IC3_LM380/NTE740A.pin14, C16_100uF_16V.+, C17_10nF.2, U4_QUAD_OP_AMP.V+
  N6: TRS1_3_5mm_Stereo_Audio_Jack_AUDIO_INPUT.Sleeve, C2_10nF.C3, R4_4_7K.Pin_1, C9.-, R10_22K.Pin_0, JACK1.NEG, C11.-, R17_4_7K.Pin_1, C11_1nF.2, C12_470pF.2, U1_500K.E, C10_0_1uF.2, C13_0_1uF.2, C4_47pF.2, C6_150pF.2, C7_2_1nF.2, IC3_LM380/NTE740A.pin3, IC3_LM380/NTE740A.pin4, IC3_LM380/NTE740A.pin5, IC3_LM380/NTE740A.pin7, IC3_LM380/NTE740A.pin10, IC3_LM380/NTE740A.pin11, IC3_LM380/NTE740A.pin12, U4_500K.E, C14_4_7uF_50V.+, C16_100uF_16V.-, C17_10nF.C3, C20_100nF.2, C21_100nF.C3, C22_100nF.2, C23_100nF.2, C19_47nF.C4#1, JACK2.NEG, U5.S, U5.E, U6_500K.S, U6_500K.E, C24_1nF.2, R29_80K.Pin_0, U7_100K.S, U7_100K.E, C28_1nF.2, U8_1Meg.S, U8_1Meg.E, R35_80K.Pin_0, TRS2_OUTPUT_FOR_25W_AMPLIFIER_BOARD.Sleeve
  N7: TRS1_3_5mm_Stereo_Audio_Jack_AUDIO_INPUT.Ring, R2_5_6K.Pin_0
  N8: TRS1_3_5mm_Stereo_Audio_Jack_AUDIO_INPUT.Tip, R1_5_6K.Pin_0
  N9: R2_5_6K.Pin_1, R1_5_6K.Pin_1, U1_500K.S
  N10: C1_10uF_25V.+, C2_10nF.2, R3_1K.Pin_1
  N11: C1_10uF_25V.-, U1_500K.A
  N12: C3_100nF.C3, R15_10K.Pin_1, IC2_LM565CN.pin2
  N13: C3_100nF.2, C8.-
  N14: C5.+, R7_10K.Pin_1, C11_1nF.C3
  N15: C5.-, C15_10uF_50V.-
  N16: R6_10K.Pin_0, R8_47K.Pin_0, IC2_LM565CN.pin7, C3_47pF.2, C4_47pF.C3
  N17: R6_10K.Pin_1, R7_10K.Pin_0, C7_2_1nF.C3
  N18: R8_47K.Pin_1, C6_150pF.C3
  N19: R9_10_ohms.Pin_0, C9.+, C11.+
  N20: R10_22K.Pin_1, U2_500K.E
  N21: R12_10_Ohms.Pin_1, R14_4_7K.Pin_0, U3_500K.S, U3_500K.E, IC2_LM565CN.pin10, C10_0_1uF.C3
  N22: R13_1K.Pin_0, IC2_LM565CN.pin8, C3_47pF.C3
  N23: R13_1K.Pin_1, U3_500K.A
  N24: R14_4_7K.Pin_1, R15_10K.Pin_0, R16_10K.Pin_0, R17_4_7K.Pin_0, C13_0_1uF.C3
  N25: R16_10K.Pin_1, IC2_LM565CN.pin3
  N26: R19_1K.Pin_1, U2_500K.A
  N27: C12_470pF.C3, IC2_LM565CN.pin9
  N28: IC2_LM565CN.pin4, IC2_LM565CN.pin5
  N29: IC3_LM380/NTE740A.pin1, C14_4_7uF_50V.-
  N30: IC3_LM380/NTE740A.pin2, U4_500K.A
  N31: IC3_LM380/NTE740A.pin8, C18_560uF.+, R20_2_7ohms.Pin_0
  N32: U4_500K.S, C15_10uF_50V.+
  N33: C18_560uF.-, R21_20Mega.Pin_0
  N34: C20_100nF.C3, R22_22Mega.Pin_1, R23_22Mega.Pin_0
  N35: C21_100nF.2, R21_20Mega.Pin_1, R22_22Mega.Pin_0
  N36: C22_100nF.C3, R23_22Mega.Pin_1, R24_22Mega.Pin_0
  N37: C23_100nF.C3, R24_22Mega.Pin_1, R26_9K.Pin_1
  N38: R20_2_7ohms.Pin_1, C19_47nF.C4#0
  N39: JACK2.POS, U4_QUAD_OP_AMP.V-
  N40: U4_QUAD_OP_AMP.OUTA, C25_1nF.C3, R27_17K.Pin_0, C26_1nF.2
  N41: U4_QUAD_OP_AMP.-INA, U5.A, R27_17K.Pin_1
  N42: U4_QUAD_OP_AMP.+INA, C24_1nF.C3, R25_9K.Pin_1
  N43: U4_QUAD_OP_AMP.+INB, R29_80K.Pin_1, C27_1nF.C3
  N44: U4_QUAD_OP_AMP.-INB, U6_500K.A, R30_160K.Pin_1
  N45: U4_QUAD_OP_AMP.OUTB, R28_82K.Pin_1, R30_160K.Pin_0, R32_8K.Pin_0
  N46: U4_QUAD_OP_AMP.OUTC, C29_1nF.C3, R31_18K.Pin_0, C30_100nF.2
  N47: U4_QUAD_OP_AMP.-INC, U7_100K.A
  N48: U4_QUAD_OP_AMP.+INC, C28_1nF.C3, R31_18K.Pin_1, R33_8K.Pin_1
  N49: U4_QUAD_OP_AMP.+IND, C31_100nF.C3, R35_80K.Pin_1
  N50: U4_QUAD_OP_AMP.-IND, U8_1Meg.A
  N51: U4_QUAD_OP_AMP.OUTD, R34_160K.Pin_0, R36_80K.Pin_1, TRS2_OUTPUT_FOR_25W_AMPLIFIER_BOARD.Ring, TRS2_OUTPUT_FOR_25W_AMPLIFIER_BOARD.Tip
  N52: C25_1nF.2, R26_9K.Pin_0, R25_9K.Pin_0
  N53: R28_82K.Pin_0, C26_1nF.C3, C27_1nF.2
  N54: C29_1nF.2, R32_8K.Pin_1, R33_8K.Pin_0
  N55: C30_100nF.C3, C31_100nF.2, R34_160K.Pin_1, R36_80K.Pin_0

notes:
  FM Modulator Demodulator, V1.0
  [25 Watts Amplifier Board]

custom parts:
  1K Ω Resistor: A generic resistor (0.25W)
  Capacitor: Capacitor Standard 0603 ceramic capacitor, and 0.1 leaded capacitor.
  Electrolytic Capacitor: A small electrolytic capacitor
  Capacitor: Capacitor Standard 0603 ceramic capacitor, and 0.1 leaded capacitor.
